// Logisim project ALU.circ as structural Verilog: 2 circuits, main circuit ALU 16-bit
module ALU_16_bit (
  input  [1:0] ALUOp,
  input  InvertA,
  input  [15:0] SrcA,
  input  [15:0] SrcB,
  input  InvertB,
  output [15:0] Result,
  output [3:0] SOCZ
);

  wire alu_1_bit_1_cout, alu_1_bit_2_cout, alu_1_bit_3_cout, alu_1_bit_4_cout, alu_1_bit_5_cout,
       alu_1_bit_6_cout, alu_1_bit_7_cout, alu_1_bit_8_cout, alu_1_bit_9_cout, alu_1_bit_10_cout,
       alu_1_bit_11_cout, alu_1_bit_12_cout, alu_1_bit_13_cout, alu_1_bit_14_cout, alu_1_bit_15_cout;

  ALU_1_bit alu_1_bit_1 (
    .SrcA(SrcA[0]), .Cin(InvertB), .SrcB(SrcB[0]), .ALUOut(Result[0]), .InvertA(InvertA), .InvertB(InvertB),
    .Cout(alu_1_bit_1_cout), .ALUOp(ALUOp));
  ALU_1_bit alu_1_bit_2 (
    .SrcA(SrcA[1]), .Cin(alu_1_bit_1_cout), .SrcB(SrcB[1]), .ALUOut(Result[1]), .InvertA(InvertA),
    .InvertB(InvertB), .Cout(alu_1_bit_2_cout), .ALUOp(ALUOp));
  ALU_1_bit alu_1_bit_3 (
    .SrcA(SrcA[2]), .Cin(alu_1_bit_2_cout), .SrcB(SrcB[2]), .ALUOut(Result[2]), .InvertA(InvertA),
    .InvertB(InvertB), .Cout(alu_1_bit_3_cout), .ALUOp(ALUOp));
  ALU_1_bit alu_1_bit_4 (
    .SrcA(SrcA[3]), .Cin(alu_1_bit_3_cout), .SrcB(SrcB[3]), .ALUOut(Result[3]), .InvertA(InvertA),
    .InvertB(InvertB), .Cout(alu_1_bit_4_cout), .ALUOp(ALUOp));
  ALU_1_bit alu_1_bit_5 (
    .SrcA(SrcA[4]), .Cin(alu_1_bit_4_cout), .SrcB(SrcB[4]), .ALUOut(Result[4]), .InvertA(InvertA),
    .InvertB(InvertB), .Cout(alu_1_bit_5_cout), .ALUOp(ALUOp));
  ALU_1_bit alu_1_bit_6 (
    .SrcA(SrcA[5]), .Cin(alu_1_bit_5_cout), .SrcB(SrcB[5]), .ALUOut(Result[5]), .InvertA(InvertA),
    .InvertB(InvertB), .Cout(alu_1_bit_6_cout), .ALUOp(ALUOp));
  ALU_1_bit alu_1_bit_7 (
    .SrcA(SrcA[6]), .Cin(alu_1_bit_6_cout), .SrcB(SrcB[6]), .ALUOut(Result[6]), .InvertA(InvertA),
    .InvertB(InvertB), .Cout(alu_1_bit_7_cout), .ALUOp(ALUOp));
  ALU_1_bit alu_1_bit_8 (
    .SrcA(SrcA[7]), .Cin(alu_1_bit_7_cout), .SrcB(SrcB[7]), .ALUOut(Result[7]), .InvertA(InvertA),
    .InvertB(InvertB), .Cout(alu_1_bit_8_cout), .ALUOp(ALUOp));
  ALU_1_bit alu_1_bit_9 (
    .SrcA(SrcA[8]), .Cin(alu_1_bit_8_cout), .SrcB(SrcB[8]), .ALUOut(Result[8]), .InvertA(InvertA),
    .InvertB(InvertB), .Cout(alu_1_bit_9_cout), .ALUOp(ALUOp));
  ALU_1_bit alu_1_bit_10 (
    .SrcA(SrcA[9]), .Cin(alu_1_bit_9_cout), .SrcB(SrcB[9]), .ALUOut(Result[9]), .InvertA(InvertA),
    .InvertB(InvertB), .Cout(alu_1_bit_10_cout), .ALUOp(ALUOp));
  ALU_1_bit alu_1_bit_11 (
    .SrcA(SrcA[10]), .Cin(alu_1_bit_10_cout), .SrcB(SrcB[10]), .ALUOut(Result[10]), .InvertA(InvertA),
    .InvertB(InvertB), .Cout(alu_1_bit_11_cout), .ALUOp(ALUOp));
  ALU_1_bit alu_1_bit_12 (
    .SrcA(SrcA[11]), .Cin(alu_1_bit_11_cout), .SrcB(SrcB[11]), .ALUOut(Result[11]), .InvertA(InvertA),
    .InvertB(InvertB), .Cout(alu_1_bit_12_cout), .ALUOp(ALUOp));
  ALU_1_bit alu_1_bit_13 (
    .SrcA(SrcA[12]), .Cin(alu_1_bit_12_cout), .SrcB(SrcB[12]), .ALUOut(Result[12]), .InvertA(InvertA),
    .InvertB(InvertB), .Cout(alu_1_bit_13_cout), .ALUOp(ALUOp));
  ALU_1_bit alu_1_bit_14 (
    .SrcA(SrcA[13]), .Cin(alu_1_bit_13_cout), .SrcB(SrcB[13]), .ALUOut(Result[13]), .InvertA(InvertA),
    .InvertB(InvertB), .Cout(alu_1_bit_14_cout), .ALUOp(ALUOp));
  ALU_1_bit alu_1_bit_15 (
    .SrcA(SrcA[14]), .Cin(alu_1_bit_14_cout), .SrcB(SrcB[14]), .ALUOut(Result[14]), .InvertA(InvertA),
    .InvertB(InvertB), .Cout(alu_1_bit_15_cout), .ALUOp(ALUOp));
  ALU_1_bit alu_1_bit_16 (
    .SrcA(SrcA[15]), .Cin(alu_1_bit_15_cout), .SrcB(SrcB[15]), .ALUOut(Result[15]), .InvertA(InvertA),
    .InvertB(InvertB), .Cout(SOCZ[1]), .ALUOp(ALUOp));
  xor Overfl (SOCZ[2], alu_1_bit_15_cout, SOCZ[1]);
  nor Zero (SOCZ[0], Result[0], Result[1], Result[2], Result[3], Result[4], Result[5], Result[6], Result[7], Result[8], Result[9], Result[10], Result[11], Result[12], Result[13], Result[14], Result[15]);
  and Sign (SOCZ[3], Result[15], ~SOCZ[1], InvertB);  // AND_Gate

  // Notes on the sheet:
  //   Carry
endmodule

module ALU_1_bit (
  input  SrcA,
  input  InvertA,
  input  Cin,
  input  SrcB,
  input  [1:0] ALUOp,
  input  InvertB,
  output ALUOut,
  output Cout
);

  wire adder_1_out, and_1_out, multiplexer_1_out, multiplexer_2_out, not_1_out, not_2_out, or_1_out,
       xor_1_out;

  not not_1 (not_1_out, SrcA);
  not not_2 (not_2_out, SrcB);
  Multiplexer #(.enable("false")) multiplexer_1 (.in0(SrcA), .in1(not_1_out), .out(multiplexer_1_out), .sel(InvertA));
  Multiplexer #(.enable("false")) multiplexer_2 (.in0(SrcB), .in1(not_2_out), .out(multiplexer_2_out), .sel(InvertB));
  and and_1 (and_1_out, multiplexer_1_out, multiplexer_2_out);
  or or_1 (or_1_out, multiplexer_1_out, multiplexer_2_out);
  xor xor_1 (xor_1_out, multiplexer_1_out, multiplexer_2_out);
  Adder #(.width(1)) adder_1 (.a(multiplexer_1_out), .b(multiplexer_2_out), .out(adder_1_out), .cin(Cin), .cout(Cout));
  Multiplexer #(.select(2), .enable("false")) multiplexer_3 (
    .in0(and_1_out), .in1(or_1_out), .in2(xor_1_out), .in3(adder_1_out), .out(ALUOut), .sel(ALUOp));
endmodule
