// Logisim project CPU.circ as structural Verilog: 1 circuit, main circuit main
module main (
);

  wire alu_control_1_inverta, alu_control_1_invertb, branch_control_1_takebranch, CLK_out,
       control_unit_1_branch, control_unit_1_memread, control_unit_1_memwrite, control_unit_1_noregsrc1,
       control_unit_1_signimm, control_unit_1_usecryptographiccore, control_unit_1_writeflags,
       control_unit_1_writeregdest, RST_out, RW_out;
  wire [1:0] alu_control_1_aluop;
  wire [3:0] alu_16_bit_1_socz, control_unit_1_control, FLAGS_q;
  wire [15:0] adder_1_out, alu_16_bit_1_result, bit_extender_1_out, bit_extender_2_out,
       cryptographic_core_1_destw, multiplexer_1_out, multiplexer_2_out, multiplexer_3_out,
       multiplexer_4_out, multiplexer_5_out, PC_q, ram_1_data, register_file_1_rd1, register_file_1_rd2,
       rom_1_data;

  Multiplexer #(.width(16), .enable("false")) multiplexer_1 (
    .in0(adder_1_out), .in1(bit_extender_1_out), .out(multiplexer_1_out), .sel(branch_control_1_takebranch));
  Register #(.width(16)) PC (.D(multiplexer_1_out), .en(1'b1), .Q(PC_q), .clk(CLK_out), .clr(RST_out));
  Clock CLK (.out(CLK_out));
  Button RST (.out(RST_out));
  Adder #(.width(16)) adder_1 (.a(16'h1), .b(PC_q), .out(adder_1_out));  // open: cin, cout
  ROM #(.addrWidth(16), .dataWidth(16)) rom_1 (.addr(PC_q), .data(rom_1_data), .sel(1'b1));
  Control_Unit control_unit_1 (
    .OPCODE(rom_1_data[15:10]), .SignImm(control_unit_1_signimm), .Branch(control_unit_1_branch),
    .WriteFlags(control_unit_1_writeflags), .WriteRegDest(control_unit_1_writeregdest),
    .NoRegSrc1(control_unit_1_noregsrc1), .MemWrite(control_unit_1_memwrite),
    .MemRead(control_unit_1_memread), .CONTROL(control_unit_1_control),
    .UseCryptographicCore(control_unit_1_usecryptographiccore));
  assign bit_extender_1_out = {{6{1'b0}}, rom_1_data[9:0]};  // Bit_Extender bit_extender_1
  Register_file register_file_1 (
    .WD3(multiplexer_4_out), .WE3(control_unit_1_writeregdest), .RST(RST_out), .A3(rom_1_data[9:8]),
    .CLK(CLK_out), .A1(rom_1_data[9:8]), .A2(rom_1_data[7:6]), .RD1(register_file_1_rd1),
    .RD2(register_file_1_rd2));
  assign bit_extender_2_out = {{8{rom_1_data[7]}}, rom_1_data[7:0]};  // Bit_Extender bit_extender_2
  Cryptographic_Core cryptographic_core_1 (
    .SrcW(register_file_1_rd2), .DestW(cryptographic_core_1_destw), .Control(control_unit_1_control));
  ALU_Control alu_control_1 (
    .ALUControl(control_unit_1_control), .InvertA(alu_control_1_inverta), .InvertB(alu_control_1_invertb),
    .ALUOp(alu_control_1_aluop));
  Multiplexer #(.width(16), .enable("false")) multiplexer_2 (
    .in0(register_file_1_rd1), .in1({16{1'b0}}), .out(multiplexer_2_out), .sel(control_unit_1_noregsrc1));
  Multiplexer #(.width(16), .enable("false")) multiplexer_3 (
    .in0(register_file_1_rd2), .in1(bit_extender_2_out), .out(multiplexer_3_out), .sel(control_unit_1_signimm));
  ALU_16_bit alu_16_bit_1 (
    .SrcA(multiplexer_2_out), .SrcB(multiplexer_3_out), .Result(alu_16_bit_1_result),
    .InvertA(alu_control_1_inverta), .ALUOp(alu_control_1_aluop), .InvertB(alu_control_1_invertb),
    .SOCZ(alu_16_bit_1_socz));
  Multiplexer #(.width(16), .disabled(0), .enable("false")) multiplexer_4 (
    .in0(multiplexer_5_out), .in1(cryptographic_core_1_destw), .out(multiplexer_4_out),
    .sel(control_unit_1_usecryptographiccore));
  Register #(.width(4)) FLAGS (
    .D(alu_16_bit_1_socz), .en(control_unit_1_writeflags), .Q(FLAGS_q), .clk(CLK_out), .clr(RST_out));
  Branch_Control branch_control_1 (
    .BranchControl(control_unit_1_control), .FLAGS_SOCZ(FLAGS_q), .Branch(control_unit_1_branch),
    .TakeBranch(branch_control_1_takebranch));
  or RW (RW_out, control_unit_1_memwrite, control_unit_1_memread);
  RAM #(.addrWidth(16), .dataWidth(16), .bus("separate")) ram_1 (
    .addr(alu_16_bit_1_result), .din(register_file_1_rd1), .data(ram_1_data), .str(control_unit_1_memwrite),
    .sel(RW_out), .clk(CLK_out), .ld(control_unit_1_memread), .clr(RST_out));
  Multiplexer #(.width(16), .enable("false")) multiplexer_5 (
    .in0(alu_16_bit_1_result), .in1(ram_1_data), .out(multiplexer_5_out), .sel(control_unit_1_memread));

  // Notes on the sheet:
  //   contents of rom_1 (hex, n*v repeats v):
  //   4d62 fd00 3a40 4c01 fe00 c100 3e40 800 c100 1d80 840c 800b d80 4c02 3240 fe00 c100 3640 800 c100
  //   1d80 8417 8016 45ff 4c03 fd00 801a
endmodule
