// Logisim project Control Unit.circ as structural Verilog: 3 circuits, main circuit Control Unit
module Control_Unit (
  input  [5:0] OPCODE,
  output SignImm,
  output Branch,
  output WriteFlags,
  output WriteRegDest,
  output NoRegSrc1,
  output MemWrite,
  output MemRead,
  output [3:0] CONTROL,
  output UseCryptographicCore
);

  wire and_1_out, decoder_1_out0, nor_1_out;

  Decoder #(.select(2), .enable("false")) decoder_1 (
    .out0(decoder_1_out0), .out1(SignImm), .out2(Branch), .out3(NoRegSrc1), .sel(OPCODE[5:4]));
  and and_1 (and_1_out, OPCODE[0], OPCODE[1], OPCODE[2], OPCODE[3]);
  nor nor_1 (nor_1_out, OPCODE[0], OPCODE[1], OPCODE[2], OPCODE[3]);
  Multiplexer #(.width(4), .disabled(0), .enable("false")) multiplexer_1 (
    .in0(OPCODE[3:0]), .in1(4'b0011), .out(CONTROL), .sel(NoRegSrc1));
  and and_2 (MemWrite, NoRegSrc1, and_1_out);
  and and_3 (MemRead, NoRegSrc1, nor_1_out);
  not not_1 (WriteFlags, Branch);
  or or_1 (WriteRegDest, decoder_1_out0, SignImm, MemRead);
  and and_4 (UseCryptographicCore, decoder_1_out0, OPCODE[2], OPCODE[3]);

  // Notes on the sheet:
  //     R-Type
  //       I-Type
  //     J-Type
  //                 R-L/S-Type
endmodule

module ALU_Control (
  input  [3:0] ALUControl,
  output InvertA,
  output InvertB,
  output [1:0] ALUOp
);


  assign ALUOp = ALUControl[1:0];
  assign InvertA = ALUControl[3];
  assign InvertB = ALUControl[2];
endmodule

module Branch_Control (
  input  [3:0] BranchControl,
  input  Branch,
  input  [3:0] FLAGS_SOCZ,
  output TakeBranch
);

  wire BNC_out, BNO_out, BNZ_out, BRC_out, BRN_out, BRO_out, BRP_out, BRZ_out, decoder_1_out0,
       decoder_1_out1, decoder_1_out2, decoder_1_out3, decoder_1_out4, decoder_1_out5, decoder_1_out6,
       decoder_1_out7, decoder_1_out8;

  Decoder #(.select(4), .tristate("true"), .disabled(0)) decoder_1 (
    .out0(decoder_1_out0), .out1(decoder_1_out1), .out2(decoder_1_out2), .out3(decoder_1_out3),
    .out4(decoder_1_out4), .out5(decoder_1_out5), .out6(decoder_1_out6), .out7(decoder_1_out7),
    .out8(decoder_1_out8), .sel(BranchControl), .en(Branch));  // open: out9, out10, out11, out12, out13, out14, out15
  and BRZ (BRZ_out, decoder_1_out1, FLAGS_SOCZ[0]);
  and BRC (BRC_out, decoder_1_out2, FLAGS_SOCZ[1]);
  and BRO (BRO_out, decoder_1_out3, FLAGS_SOCZ[2]);
  and BRN (BRN_out, decoder_1_out4, FLAGS_SOCZ[3]);
  and BNZ (BNZ_out, decoder_1_out5, ~FLAGS_SOCZ[0]);  // AND_Gate
  and BNC (BNC_out, decoder_1_out6, ~FLAGS_SOCZ[1]);  // AND_Gate
  and BNO (BNO_out, decoder_1_out7, ~FLAGS_SOCZ[2]);  // AND_Gate
  and BRP (BRP_out, decoder_1_out8, ~FLAGS_SOCZ[3]);  // AND_Gate
  Multiplexer #(.select(4), .disabled(0)) multiplexer_1 (
    .in0(decoder_1_out0), .in1(BRZ_out), .in2(BRC_out), .in3(BRO_out), .in4(BRN_out), .in5(BNZ_out),
    .in6(BNC_out), .in7(BNO_out), .in8(BRP_out), .out(TakeBranch), .sel(BranchControl), .en(Branch));  // open: in9, in10, in11, in12, in13, in14, in15

  // Notes on the sheet:
  //   S
  //   O
  //   C
  //   Z
  //   BRA
  //   BRZ
  //   BRC
  //   BRO
  //   BRN
  //   BNZ
  //   BNC
  //   BNO
  //   BRP
endmodule
