// Logisim project Cryptographic Units.circ as structural Verilog: 6 circuits, main circuit Cryptographic Control Unit
module Cryptographic_Control_Unit (
  input  [3:0] Control,
  output Decrypt,
  output UseCC,
  output UseB64
);

  not not_1 (UseB64, Control[1]);

  assign Decrypt = Control[0];
  assign UseCC = Control[1];
endmodule

module Caesar_s_Cypher_Core (
  input  [7:0] InputChar,
  input  Decrypt,
  output [7:0] OutputChar
);

  wire comparator_1_gt, comparator_2_gt;
  wire [7:0] adder_1_out, multiplexer_1_out, multiplexer_2_out, multiplexer_3_out, multiplexer_4_out,
       multiplexer_5_out, multiplexer_6_out, multiplexer_7_out, not_1_out, subtractor_1_out;

  Comparator comparator_1 (.a(InputChar), .b(8'h60), .gt(comparator_1_gt));  // open: eq, lt
  Subtractor subtractor_1 (.a(InputChar), .b(multiplexer_1_out), .out(subtractor_1_out));  // open: bin, bout
  Multiplexer #(.width(8), .enable("false")) multiplexer_1 (
    .in0(8'h41), .in1(8'h61), .out(multiplexer_1_out), .sel(comparator_1_gt));
  Comparator #(.mode("unsigned")) comparator_2 (
    .a(subtractor_1_out), .b(multiplexer_2_out), .gt(comparator_2_gt));  // open: eq, lt
  Multiplexer #(.width(8), .disabled(0), .enable("false")) multiplexer_2 (
    .in0(8'h2), .in1(8'h16), .out(multiplexer_2_out), .sel(Decrypt));
  Multiplexer #(.width(8), .disabled(0), .enable("false")) multiplexer_3 (
    .in0(8'h17), .in1(8'h3), .out(multiplexer_3_out), .sel(Decrypt));
  Multiplexer #(.width(8), .disabled(0), .enable("false")) multiplexer_4 (
    .in0(8'h3), .in1(8'h17), .out(multiplexer_4_out), .sel(Decrypt));
  Multiplexer #(.width(8), .disabled(0), .enable("false")) multiplexer_5 (
    .in0(multiplexer_3_out), .in1(multiplexer_4_out), .out(multiplexer_5_out), .sel(comparator_2_gt));
  Multiplexer #(.width(8), .disabled(0), .enable("false")) multiplexer_6 (
    .in0(multiplexer_5_out), .in1(not_1_out), .out(multiplexer_6_out), .sel(comparator_2_gt));
  assign not_1_out = ~multiplexer_5_out;  // NOT_Gate not_1, 8 bits wide
  Adder adder_1 (.a(subtractor_1_out), .b(multiplexer_6_out), .out(adder_1_out), .cin(comparator_2_gt));  // open: cout
  Multiplexer #(.width(8), .enable("false")) multiplexer_7 (
    .in0(8'h41), .in1(8'h61), .out(multiplexer_7_out), .sel(comparator_1_gt));
  Adder adder_2 (.a(adder_1_out), .b(multiplexer_7_out), .out(OutputChar));  // open: cin, cout

  // Notes on the sheet:
  //   'A'
  //   'a'
endmodule

module Base64_Core (
  input  Decrypt,
  input  [15:0] InputWord,
  output [15:0] OutputWord
);

  wire [5:0] ascii_to_b64_1_b64code, ascii_to_b64_2_b64code;
  wire [7:0] b64_to_ascii_1_ascii, b64_to_ascii_2_ascii;

  ASCII_To_B64 ascii_to_b64_1 (.ASCII(InputWord[7:0]), .B64Code(ascii_to_b64_1_b64code));
  ASCII_To_B64 ascii_to_b64_2 (.ASCII(InputWord[15:8]), .B64Code(ascii_to_b64_2_b64code));
  B64_To_ASCII b64_to_ascii_1 (.B64Code(InputWord[7:2]), .ASCII(b64_to_ascii_1_ascii));
  B64_To_ASCII b64_to_ascii_2 (.B64Code({InputWord[1:0], 4'b0000}), .ASCII(b64_to_ascii_2_ascii));
  Multiplexer #(.width(16), .disabled(0), .enable("false")) multiplexer_1 (
    .in0({b64_to_ascii_1_ascii, b64_to_ascii_2_ascii}),
    .in1({{8{1'b0}}, ascii_to_b64_2_b64code, ascii_to_b64_1_b64code[5:4]}), .out(OutputWord), .sel(Decrypt));
  // Probe on OutputWord
endmodule

module B64_To_ASCII (
  input  [5:0] B64Code,
  output [7:0] ASCII
);

  wire comparator_1_gt, comparator_2_gt, comparator_3_eq, comparator_4_eq, priority_encoder_1_gs;
  wire [1:0] priority_encoder_1_out;
  wire [7:0] adder_1_out, adder_2_out, bit_extender_1_out, multiplexer_1_out, subtractor_1_out;

  assign bit_extender_1_out = {{2{1'b0}}, B64Code};  // Bit_Extender bit_extender_1
  Adder adder_1 (.a(bit_extender_1_out), .b(8'h41), .out(adder_1_out));  // open: cin, cout
  Adder adder_2 (.a(bit_extender_1_out), .b(8'h47), .out(adder_2_out));  // open: cin, cout
  Subtractor subtractor_1 (.a(bit_extender_1_out), .b(8'h4), .out(subtractor_1_out));  // open: bin, bout
  Comparator #(.mode("unsigned")) comparator_1 (
    .a(bit_extender_1_out), .b(8'h19), .gt(comparator_1_gt));  // open: eq, lt
  Comparator #(.mode("unsigned")) comparator_2 (
    .a(bit_extender_1_out), .b(8'h33), .gt(comparator_2_gt));  // open: eq, lt
  Comparator #(.mode("unsigned")) comparator_3 (
    .a(bit_extender_1_out), .b(8'h3e), .eq(comparator_3_eq));  // open: gt, lt
  Comparator #(.mode("unsigned")) comparator_4 (
    .a(bit_extender_1_out), .b(8'h3f), .eq(comparator_4_eq));  // open: gt, lt
  Multiplexer #(.select(2), .width(8), .disabled(0)) multiplexer_1 (
    .in0(adder_2_out), .in1(subtractor_1_out), .in2(8'h2b), .in3(8'h2f), .out(multiplexer_1_out),
    .sel(priority_encoder_1_out), .en(priority_encoder_1_gs));
  Priority_Encoder #(.select(2)) priority_encoder_1 (
    .in0(comparator_1_gt), .in1(comparator_2_gt), .in2(comparator_3_eq), .in3(comparator_4_eq),
    .out(priority_encoder_1_out), .gs(priority_encoder_1_gs));  // open: en_out, en_in
  Multiplexer #(.width(8), .enable("false")) multiplexer_2 (
    .in0(adder_1_out), .in1(multiplexer_1_out), .out(ASCII), .sel(priority_encoder_1_gs));

  // Notes on the sheet:
  //   'a' - 0x1a
  //   '0' - 0x34
  //   'A'
  //   '+'
  //   IF lowercase
  //   IF digit
  //   IF '+'
  //   IF '/'
  //   '/'
endmodule

module ASCII_To_B64 (
  input  [7:0] ASCII,
  output [5:0] B64Code
);

  wire comparator_1_lt, comparator_2_gt, comparator_3_eq, comparator_4_eq, priority_encoder_1_gs;
  wire [1:0] priority_encoder_1_out;
  wire [7:0] adder_1_out, multiplexer_1_out, multiplexer_2_out, subtractor_1_out, subtractor_2_out;

  Subtractor subtractor_1 (.a(ASCII), .b(8'h41), .out(subtractor_1_out));  // open: bin, bout
  Adder adder_1 (.a(ASCII), .b(8'h4), .out(adder_1_out));  // open: cin, cout
  Subtractor subtractor_2 (.a(ASCII), .b(8'h47), .out(subtractor_2_out));  // open: bin, bout
  Comparator #(.mode("unsigned")) comparator_1 (.a(ASCII), .b(8'h3a), .lt(comparator_1_lt));  // open: gt, eq
  Comparator #(.mode("unsigned")) comparator_2 (.a(ASCII), .b(8'h60), .gt(comparator_2_gt));  // open: eq, lt
  Comparator #(.mode("unsigned")) comparator_3 (.a(ASCII), .b(8'h2f), .eq(comparator_3_eq));  // open: gt, lt
  Comparator #(.mode("unsigned")) comparator_4 (.a(ASCII), .b(8'h2b), .eq(comparator_4_eq));  // open: gt, lt
  Priority_Encoder #(.select(2)) priority_encoder_1 (
    .in0(comparator_1_lt), .in1(comparator_2_gt), .in2(comparator_3_eq), .in3(comparator_4_eq),
    .out(priority_encoder_1_out), .gs(priority_encoder_1_gs));  // open: en_out, en_in
  Multiplexer #(.select(2), .width(8), .disabled(0)) multiplexer_1 (
    .in0(adder_1_out), .in1(subtractor_2_out), .in2(8'h3f), .in3(8'h3e), .out(multiplexer_1_out),
    .sel(priority_encoder_1_out), .en(priority_encoder_1_gs));
  Bit_Extender #(.out_width(6)) bit_extender_1 (.in(multiplexer_2_out), .out(B64Code));
  Multiplexer #(.width(8), .enable("false")) multiplexer_2 (
    .in0(subtractor_1_out), .in1(multiplexer_1_out), .out(multiplexer_2_out), .sel(priority_encoder_1_gs));

  // Notes on the sheet:
  //   'A'
  //   0x34 - '0'
  //   'a' - 0x1a
  //                    IF digit
  //                    IF lowercase
  //       IF '/'
  //        IF '+'
endmodule

module Cryptographic_Core (
  input  [3:0] Control,
  input  [15:0] SrcW,
  output [15:0] DestW
);

  wire cryptographic_control_unit_1_decrypt, cryptographic_control_unit_1_useb64,
       cryptographic_control_unit_1_usecc, priority_encoder_1_out;
  wire [7:0] caesar_s_cypher_core_1_outputchar;
  wire [15:0] base64_core_1_outputword, bit_extender_1_out;

  Cryptographic_Control_Unit cryptographic_control_unit_1 (
    .Control(Control), .Decrypt(cryptographic_control_unit_1_decrypt),
    .UseCC(cryptographic_control_unit_1_usecc), .UseB64(cryptographic_control_unit_1_useb64));
  Priority_Encoder #(.select(1)) priority_encoder_1 (
    .in0(cryptographic_control_unit_1_usecc), .in1(cryptographic_control_unit_1_useb64),
    .out(priority_encoder_1_out));  // open: gs, en_out, en_in
  Caesar_s_Cypher_Core caesar_s_cypher_core_1 (
    .InputChar(SrcW[7:0]), .OutputChar(caesar_s_cypher_core_1_outputchar),
    .Decrypt(cryptographic_control_unit_1_decrypt));
  assign bit_extender_1_out = {{8{1'b0}}, caesar_s_cypher_core_1_outputchar};  // Bit_Extender bit_extender_1
  Base64_Core base64_core_1 (
    .InputWord(SrcW), .OutputWord(base64_core_1_outputword), .Decrypt(cryptographic_control_unit_1_decrypt));
  Multiplexer #(.width(16), .disabled(0), .enable("false")) multiplexer_1 (
    .in0(bit_extender_1_out), .in1(base64_core_1_outputword), .out(DestW), .sel(priority_encoder_1_out));
endmodule
