// Logisim project Register File.circ as structural Verilog: 1 circuit, main circuit Register file
module Register_file (
  input  WE3,
  input  RST,
  input  [1:0] A1,
  input  [1:0] A3,
  input  [1:0] A2,
  input  [15:0] WD3,
  input  CLK,
  output [15:0] RD1,
  output [15:0] RD2
);

  wire and_1_out, and_2_out, and_3_out, and_4_out, decoder_1_out0, decoder_1_out1, decoder_1_out2,
       decoder_1_out3;
  wire [15:0] ACC_q, SP_q, X_q, Y_q;

  Decoder #(.select(2), .enable("false")) decoder_1 (
    .out0(decoder_1_out0), .out1(decoder_1_out1), .out2(decoder_1_out2), .out3(decoder_1_out3), .sel(A3));
  and and_1 (and_1_out, decoder_1_out0, WE3);
  and and_2 (and_2_out, decoder_1_out1, WE3);
  and and_3 (and_3_out, decoder_1_out2, WE3);
  and and_4 (and_4_out, decoder_1_out3, WE3);
  Register #(.width(16)) ACC (.D(WD3), .en(and_1_out), .Q(ACC_q), .clk(CLK), .clr(RST));
  Register #(.width(16)) X (.D(WD3), .en(and_2_out), .Q(X_q), .clk(CLK), .clr(RST));
  Register #(.width(16)) Y (.D(WD3), .en(and_3_out), .Q(Y_q), .clk(CLK), .clr(RST));
  Register #(.width(16)) SP (.D(WD3), .en(and_4_out), .Q(SP_q), .clk(CLK), .clr(RST));
  Multiplexer #(.select(2), .width(16), .enable("false")) multiplexer_1 (
    .in0(ACC_q), .in1(X_q), .in2(Y_q), .in3(SP_q), .out(RD1), .sel(A1));
  Multiplexer #(.select(2), .width(16), .enable("false")) multiplexer_2 (
    .in0(ACC_q), .in1(X_q), .in2(Y_q), .in3(SP_q), .out(RD2), .sel(A2));
endmodule
